// Logisim project 01.02.24.circ as structural Verilog: 6 circuits, main circuit 5.1
module _5_1 (
  input  s,
  input  r,
  input  c,
  input  r_2,
  input  s_2,
  input  in_6,
  output q,
  output q_2,
  output minus_q,
  output minus_q_2
);

  wire nand_3_out, nand_4_out;

  nand nand_1 (q, s, minus_q);
  nand nand_2 (minus_q, q, r_2);
  nand nand_3 (nand_3_out, r, c);
  nand nand_4 (nand_4_out, c, s_2);
  nand nand_5 (q_2, nand_3_out, minus_q_2);
  nand nand_6 (minus_q_2, q_2, nand_4_out);

  // Notes on the sheet:
  //   5.1 #1
  //   rs триггер
  //   на элементах и
  //   5.1 #2
  //   синхронный rs
endmodule

module _5_2_4 (
  input  x,
  input  y,
  input  z,
  output out_4
);

  wire and_1_out, and_2_out, not_1_out, not_2_out, or_1_out;

  not not_1 (not_1_out, x);
  and and_1 (and_1_out, not_1_out, y);
  and and_2 (and_2_out, and_1_out, z);
  or or_1 (or_1_out, y, and_2_out);
  not not_2 (not_2_out, y);
  and and_3 (out_4, not_2_out, or_1_out);
endmodule

module \_5_2_6_хрень  (
  input  j,
  input  c,
  input  k,
  output q,
  output minus_q
);

  wire nand_1_out, nand_2_out, nand_3_out, nand_4_out, nand_5_out, nand_6_out;

  nand nand_1 (nand_1_out, minus_q, j, c);
  nand nand_2 (nand_2_out, c, k, q);
  nand nand_3 (nand_3_out, nand_1_out, nand_4_out);
  nand nand_4 (nand_4_out, nand_3_out, nand_2_out);
  nand nand_5 (nand_5_out, nand_1_out, nand_3_out);
  nand nand_6 (nand_6_out, nand_4_out, nand_2_out);
  not nand_7 (q, minus_q);  // NAND_Gate
  not nand_8 (minus_q, q);  // NAND_Gate

  // Notes on the sheet:
  //   jk
endmodule

module _5_2_5 (
  input  r,
  input  c,
  input  s,
  output q,
  output minus_q
);

  wire and_1_out, and_2_out;

  and and_1 (and_1_out, r, c);
  and and_2 (and_2_out, c, s);
  xnor xnor_1 (q, and_1_out, minus_q);
  xnor xnor_2 (minus_q, q, and_2_out);

  // Notes on the sheet:
  //   5.2 #5
  //   aсинхр rs
endmodule

module _5_2_2 (
  input  x,
  input  y,
  output out_3
);

  wire and_1_out, and_2_out, not_1_out, not_2_out;

  not not_1 (not_1_out, x);
  not not_2 (not_2_out, y);
  and and_1 (and_1_out, not_1_out, y);
  and and_2 (and_2_out, x, not_2_out);
  or or_1 (out_3, and_1_out, and_2_out);

  // Notes on the sheet:
  //   5.2 #2
  //   схема искл или
endmodule

module _5_2_3 (
  input  s,
  input  r,
  output q,
  output minus_q
);

  nor nor_1 (q, s, minus_q);
  nor nor_2 (minus_q, q, r);

  // Notes on the sheet:
  //   5.2 #3
  //   rs триггер
endmodule
