// Logisim project 08.02.24 регистрвы + счетчики.circ as structural Verilog: 5 circuits, main circuit #1
module _1 (
  input  \П ,
  input  x1,
  input  x2,
  input  x3,
  input  x4,
  input  \Bпр ,
  input  \Вобр ,
  output out_8,
  output out_9,
  output out_10,
  output out_11
);

  wire and_1_out, and_2_out, and_3_out, and_4_out, and_5_out, and_6_out, and_7_out, and_8_out, d_ff_1_q,
       d_ff_1_qn, d_ff_2_q, d_ff_2_qn, d_ff_3_q, d_ff_3_qn, d_ff_4_q, d_ff_4_qn;

  D_Flip_Flop d_ff_1 (.clk(\П ), .D(x1), .Q(d_ff_1_q), .Qn(d_ff_1_qn));  // open: preset, en, reset
  D_Flip_Flop d_ff_2 (.clk(\П ), .D(x2), .Q(d_ff_2_q), .Qn(d_ff_2_qn));  // open: preset, en, reset
  D_Flip_Flop d_ff_3 (.clk(\П ), .D(x3), .Q(d_ff_3_q), .Qn(d_ff_3_qn));  // open: preset, en, reset
  D_Flip_Flop d_ff_4 (.clk(\П ), .D(x4), .Q(d_ff_4_q), .Qn(d_ff_4_qn));  // open: preset, en, reset
  and and_1 (and_1_out, \Bпр , d_ff_1_q);
  and and_2 (and_2_out, \Bпр , d_ff_2_q);
  and and_3 (and_3_out, \Bпр , d_ff_3_q);
  and and_4 (and_4_out, \Bпр , d_ff_4_q);
  and and_5 (and_5_out, d_ff_1_qn, \Вобр );
  and and_6 (and_6_out, d_ff_2_qn, \Вобр );
  and and_7 (and_7_out, d_ff_3_qn, \Вобр );
  and and_8 (and_8_out, d_ff_4_qn, \Вобр );
  or or_1 (out_8, and_1_out, and_5_out);
  or or_2 (out_9, and_2_out, and_6_out);
  or or_3 (out_10, and_3_out, and_7_out);
  or or_4 (out_11, and_4_out, and_8_out);

  // Notes on the sheet:
  //   101
  //   1024
endmodule

module _2 (
  input  in,
  input  trig,
  output out_3,
  output out_4,
  output out_5,
  output out_6
);

  D_Flip_Flop d_ff_1 (.clk(trig), .D(in), .Q(out_3));  // open: Qn, preset, en, reset
  D_Flip_Flop d_ff_2 (.clk(trig), .D(out_3), .Q(out_4));  // open: Qn, preset, en, reset
  D_Flip_Flop d_ff_3 (.clk(trig), .D(out_4), .Q(out_5));  // open: Qn, preset, en, reset
  D_Flip_Flop d_ff_4 (.clk(trig), .D(out_5), .Q(out_6));  // open: Qn, preset, en, reset

  // Notes on the sheet:
  //   100
endmodule

module _111 (
  input  \П ,
  input  \Bпр ,
  input  \Вобр ,
  input  in_4,
  output out_5,
  output out_6,
  output out_7,
  output out_8,
  output out_9,
  output out_10,
  output out_11,
  output out_12
);

  wire and_1_out, and_2_out, and_3_out, and_4_out, and_5_out, and_6_out, and_7_out, and_8_out, and_9_out,
       and_10_out, and_11_out, and_12_out, and_13_out, and_14_out, and_15_out, and_16_out, button_1_out,
       clock_1_out, d_ff_1_q, d_ff_1_qn, d_ff_2_q, d_ff_2_qn, d_ff_3_q, d_ff_3_qn, d_ff_4_q, d_ff_4_qn,
       d_ff_5_q, d_ff_5_qn, d_ff_6_q, d_ff_6_qn, d_ff_7_q, d_ff_7_qn, d_ff_8_q, d_ff_8_qn, t_ff_1_q,
       t_ff_1_qn, t_ff_2_q, t_ff_2_qn, t_ff_3_q, t_ff_3_qn, t_ff_4_q, t_ff_4_qn, t_ff_5_q, t_ff_5_qn,
       t_ff_6_q, t_ff_6_qn, t_ff_7_q, t_ff_7_qn, t_ff_8_q;

  Clock clock_1 (.out(clock_1_out));
  Button button_1 (.out(button_1_out));
  LED led_1 (.in(t_ff_1_q));
  T_Flip_Flop t_ff_1 (
    .clk(clock_1_out), .T(in_4), .Q(t_ff_1_q), .Qn(t_ff_1_qn), .reset(button_1_out));  // open: preset, en
  D_Flip_Flop d_ff_1 (.clk(\П ), .D(t_ff_8_q), .Q(d_ff_1_q), .Qn(d_ff_1_qn));  // open: preset, en, reset
  D_Flip_Flop d_ff_2 (.clk(\П ), .D(t_ff_7_q), .Q(d_ff_2_q), .Qn(d_ff_2_qn));  // open: preset, en, reset
  D_Flip_Flop d_ff_3 (.clk(\П ), .D(t_ff_6_q), .Q(d_ff_3_q), .Qn(d_ff_3_qn));  // open: preset, en, reset
  D_Flip_Flop d_ff_4 (.clk(\П ), .D(t_ff_5_q), .Q(d_ff_4_q), .Qn(d_ff_4_qn));  // open: preset, en, reset
  D_Flip_Flop d_ff_5 (.clk(\П ), .D(t_ff_4_q), .Q(d_ff_5_q), .Qn(d_ff_5_qn));  // open: preset, en, reset
  D_Flip_Flop d_ff_6 (.clk(\П ), .D(t_ff_3_q), .Q(d_ff_6_q), .Qn(d_ff_6_qn));  // open: preset, en, reset
  D_Flip_Flop d_ff_7 (.clk(\П ), .D(t_ff_2_q), .Q(d_ff_7_q), .Qn(d_ff_7_qn));  // open: preset, en, reset
  D_Flip_Flop d_ff_8 (.clk(\П ), .D(t_ff_1_q), .Q(d_ff_8_q), .Qn(d_ff_8_qn));  // open: preset, en, reset
  LED led_2 (.in(t_ff_2_q));
  T_Flip_Flop t_ff_2 (
    .clk(t_ff_1_qn), .T(in_4), .Q(t_ff_2_q), .Qn(t_ff_2_qn), .reset(button_1_out));  // open: preset, en
  LED led_3 (.in(t_ff_3_q));
  T_Flip_Flop t_ff_3 (
    .clk(t_ff_2_qn), .T(in_4), .Q(t_ff_3_q), .Qn(t_ff_3_qn), .reset(button_1_out));  // open: preset, en
  and and_1 (and_1_out, \Bпр , d_ff_1_q);
  and and_2 (and_2_out, \Bпр , d_ff_2_q);
  and and_3 (and_3_out, \Bпр , d_ff_3_q);
  and and_4 (and_4_out, \Bпр , d_ff_4_q);
  and and_5 (and_5_out, \Bпр , d_ff_5_q);
  and and_6 (and_6_out, \Bпр , d_ff_6_q);
  and and_7 (and_7_out, \Bпр , d_ff_7_q);
  and and_8 (and_8_out, \Bпр , d_ff_8_q);
  LED led_4 (.in(t_ff_4_q));
  T_Flip_Flop t_ff_4 (
    .clk(t_ff_3_qn), .T(in_4), .Q(t_ff_4_q), .Qn(t_ff_4_qn), .reset(button_1_out));  // open: preset, en
  and and_9 (and_9_out, d_ff_1_qn, \Вобр );
  and and_10 (and_10_out, d_ff_2_qn, \Вобр );
  and and_11 (and_11_out, d_ff_3_qn, \Вобр );
  and and_12 (and_12_out, d_ff_4_qn, \Вобр );
  and and_13 (and_13_out, d_ff_5_qn, \Вобр );
  and and_14 (and_14_out, d_ff_6_qn, \Вобр );
  and and_15 (and_15_out, d_ff_7_qn, \Вобр );
  and and_16 (and_16_out, d_ff_8_qn, \Вобр );
  LED led_5 (.in(t_ff_5_q));
  T_Flip_Flop t_ff_5 (
    .clk(t_ff_4_qn), .T(in_4), .Q(t_ff_5_q), .Qn(t_ff_5_qn), .reset(button_1_out));  // open: preset, en
  or or_1 (out_5, and_1_out, and_9_out);
  or or_2 (out_6, and_2_out, and_10_out);
  or or_3 (out_7, and_3_out, and_11_out);
  or or_4 (out_8, and_4_out, and_12_out);
  or or_5 (out_9, and_5_out, and_13_out);
  or or_6 (out_10, and_6_out, and_14_out);
  or or_7 (out_11, and_7_out, and_15_out);
  or or_8 (out_12, and_8_out, and_16_out);
  T_Flip_Flop t_ff_6 (
    .clk(t_ff_5_qn), .T(in_4), .Q(t_ff_6_q), .Qn(t_ff_6_qn), .reset(button_1_out));  // open: preset, en
  LED led_6 (.in(t_ff_6_q));
  LED led_7 (.in(t_ff_7_q));
  T_Flip_Flop t_ff_7 (
    .clk(t_ff_6_qn), .T(in_4), .Q(t_ff_7_q), .Qn(t_ff_7_qn), .reset(button_1_out));  // open: preset, en
  LED led_8 (.in(t_ff_8_q));
  T_Flip_Flop t_ff_8 (.clk(t_ff_7_qn), .T(in_4), .Q(t_ff_8_q), .reset(button_1_out));  // open: Qn, preset, en

  // Notes on the sheet:
  //   101
  //   1024
endmodule

module _222__1 (
  input  in_1,
  output out_2,
  output out_3,
  output out_4
);

  wire button_1_out, clock_1_out, t_ff_1_q, t_ff_1_qn, t_ff_2_q, t_ff_2_qn, t_ff_3_q, t_ff_3_qn, t_ff_4_q,
       t_ff_4_qn, t_ff_5_q, t_ff_5_qn, t_ff_6_q, t_ff_6_qn, t_ff_7_q, t_ff_7_qn, t_ff_8_q;

  Clock clock_1 (.out(clock_1_out));
  Button button_1 (.out(button_1_out));
  LED led_1 (.in(t_ff_1_q));
  T_Flip_Flop t_ff_1 (
    .clk(clock_1_out), .T(in_1), .Q(t_ff_1_q), .Qn(t_ff_1_qn), .reset(button_1_out));  // open: preset, en
  LED led_2 (.in(t_ff_2_q));
  T_Flip_Flop t_ff_2 (
    .clk(t_ff_1_qn), .T(in_1), .Q(t_ff_2_q), .Qn(t_ff_2_qn), .reset(button_1_out));  // open: preset, en
  LED led_3 (.in(t_ff_3_q));
  T_Flip_Flop t_ff_3 (
    .clk(t_ff_2_qn), .T(in_1), .Q(t_ff_3_q), .Qn(t_ff_3_qn), .reset(button_1_out));  // open: preset, en
  LED led_4 (.in(t_ff_4_q));
  T_Flip_Flop t_ff_4 (
    .clk(t_ff_3_qn), .T(in_1), .Q(t_ff_4_q), .Qn(t_ff_4_qn), .reset(button_1_out));  // open: preset, en
  LED led_5 (.in(t_ff_5_q));
  T_Flip_Flop t_ff_5 (
    .clk(t_ff_4_qn), .T(in_1), .Q(t_ff_5_q), .Qn(t_ff_5_qn), .reset(button_1_out));  // open: preset, en
  T_Flip_Flop t_ff_6 (
    .clk(t_ff_5_qn), .T(in_1), .Q(t_ff_6_q), .Qn(t_ff_6_qn), .reset(button_1_out));  // open: preset, en
  LED led_6 (.in(t_ff_6_q));
  LED led_7 (.in(t_ff_7_q));
  T_Flip_Flop t_ff_7 (
    .clk(t_ff_6_qn), .T(in_1), .Q(t_ff_7_q), .Qn(t_ff_7_qn), .reset(button_1_out));  // open: preset, en
  LED led_8 (.in(t_ff_8_q));
  T_Flip_Flop t_ff_8 (.clk(t_ff_7_qn), .T(in_1), .Q(t_ff_8_q), .reset(button_1_out));  // open: Qn, preset, en
  or or_1 (out_2, t_ff_2_q, t_ff_4_q, t_ff_6_q, t_ff_8_q);
  or or_2 (out_3, t_ff_3_q, t_ff_4_q, t_ff_7_q, t_ff_8_q);
  or or_3 (out_4, t_ff_5_q, t_ff_6_q, t_ff_7_q, t_ff_8_q);
endmodule

module _222__2 (
  input  in_1,
  input  in_2,
  input  in_3,
  input  in_4,
  input  in_5,
  output out_6
);

  wire _1_out, _2_out, _3_out, _4_out, _5_out, _6_out, _7_out, _8_out, button_1_out, clock_1_out, not_1_out,
       not_2_out, not_3_out, not_4_out, not_5_out, not_6_out, not_7_out, t_ff_1_q, t_ff_1_qn, t_ff_2_q,
       t_ff_2_qn, t_ff_3_q, t_ff_3_qn, t_ff_4_q, t_ff_4_qn, t_ff_5_q, t_ff_5_qn, t_ff_6_q, t_ff_6_qn,
       t_ff_7_q, t_ff_7_qn, t_ff_8_q;

  not not_1 (not_1_out, in_2);
  not not_2 (not_2_out, in_3);
  not not_3 (not_3_out, in_4);
  Clock clock_1 (.out(clock_1_out));
  Button button_1 (.out(button_1_out));
  not not_4 (not_4_out, in_1);
  not not_5 (not_5_out, not_1_out);
  not not_6 (not_6_out, not_2_out);
  not not_7 (not_7_out, not_3_out);
  LED led_1 (.in(t_ff_1_q));
  T_Flip_Flop t_ff_1 (
    .clk(clock_1_out), .T(in_5), .Q(t_ff_1_q), .Qn(t_ff_1_qn), .reset(button_1_out));  // open: preset, en
  LED led_2 (.in(t_ff_2_q));
  T_Flip_Flop t_ff_2 (
    .clk(t_ff_1_qn), .T(in_5), .Q(t_ff_2_q), .Qn(t_ff_2_qn), .reset(button_1_out));  // open: preset, en
  LED led_3 (.in(t_ff_3_q));
  T_Flip_Flop t_ff_3 (
    .clk(t_ff_2_qn), .T(in_5), .Q(t_ff_3_q), .Qn(t_ff_3_qn), .reset(button_1_out));  // open: preset, en
  LED led_4 (.in(t_ff_4_q));
  T_Flip_Flop t_ff_4 (
    .clk(t_ff_3_qn), .T(in_5), .Q(t_ff_4_q), .Qn(t_ff_4_qn), .reset(button_1_out));  // open: preset, en
  LED led_5 (.in(t_ff_5_q));
  T_Flip_Flop t_ff_5 (
    .clk(t_ff_4_qn), .T(in_5), .Q(t_ff_5_q), .Qn(t_ff_5_qn), .reset(button_1_out));  // open: preset, en
  LED led_6 (.in(t_ff_6_q));
  T_Flip_Flop t_ff_6 (
    .clk(t_ff_5_qn), .T(in_5), .Q(t_ff_6_q), .Qn(t_ff_6_qn), .reset(button_1_out));  // open: preset, en
  LED led_7 (.in(t_ff_7_q));
  T_Flip_Flop t_ff_7 (
    .clk(t_ff_6_qn), .T(in_5), .Q(t_ff_7_q), .Qn(t_ff_7_qn), .reset(button_1_out));  // open: preset, en
  T_Flip_Flop t_ff_8 (.clk(t_ff_7_qn), .T(in_5), .Q(t_ff_8_q), .reset(button_1_out));  // open: Qn, preset, en
  LED led_8 (.in(t_ff_8_q));
  and _1 (_1_out, t_ff_1_q, not_1_out, not_2_out, not_3_out, not_4_out);
  and _2 (_2_out, t_ff_2_q, not_5_out, not_2_out, not_3_out, not_4_out);
  and _3 (_3_out, t_ff_3_q, not_1_out, not_6_out, not_3_out, not_4_out);
  and _4 (_4_out, t_ff_4_q, not_5_out, not_6_out, not_3_out, not_4_out);
  and _5 (_5_out, t_ff_5_q, not_1_out, not_2_out, not_7_out, not_4_out);
  and _6 (_6_out, t_ff_6_q, not_5_out, not_2_out, not_7_out, not_4_out);
  and _7 (_7_out, t_ff_7_q, not_1_out, not_6_out, not_7_out, not_4_out);
  and _8 (_8_out, t_ff_8_q, not_5_out, not_6_out, not_7_out, not_4_out);
  or or_1 (out_6, _1_out, _2_out, _3_out, _4_out, _5_out, _6_out, _7_out, _8_out);
endmodule
