// Logisim project 08.02.24 счетчики.circ as structural Verilog: 2 circuits, main circuit main
module main (
  input  in_1,
  output out_2,
  output out_3,
  output out_4,
  output out_5,
  output out_6,
  output out_7,
  output out_8,
  output out_9
);

  wire button_1_out, clock_1_out, t_ff_1_qn, t_ff_2_qn, t_ff_3_qn, t_ff_4_qn, t_ff_5_qn, t_ff_6_qn, t_ff_7_qn;

  Clock clock_1 (.out(clock_1_out));
  Button button_1 (.out(button_1_out));
  T_Flip_Flop t_ff_1 (
    .clk(clock_1_out), .T(in_1), .Q(out_2), .Qn(t_ff_1_qn), .reset(button_1_out));  // open: preset, en
  T_Flip_Flop t_ff_2 (.clk(t_ff_1_qn), .T(in_1), .Q(out_3), .Qn(t_ff_2_qn), .reset(button_1_out));  // open: preset, en
  T_Flip_Flop t_ff_3 (.clk(t_ff_2_qn), .T(in_1), .Q(out_4), .Qn(t_ff_3_qn), .reset(button_1_out));  // open: preset, en
  T_Flip_Flop t_ff_4 (.clk(t_ff_3_qn), .T(in_1), .Q(out_5), .Qn(t_ff_4_qn), .reset(button_1_out));  // open: preset, en
  T_Flip_Flop t_ff_5 (.clk(t_ff_4_qn), .T(in_1), .Q(out_6), .Qn(t_ff_5_qn), .reset(button_1_out));  // open: preset, en
  T_Flip_Flop t_ff_6 (.clk(t_ff_5_qn), .T(in_1), .Q(out_7), .Qn(t_ff_6_qn), .reset(button_1_out));  // open: preset, en
  T_Flip_Flop t_ff_7 (.clk(t_ff_6_qn), .T(in_1), .Q(out_8), .Qn(t_ff_7_qn), .reset(button_1_out));  // open: preset, en
  T_Flip_Flop t_ff_8 (.clk(t_ff_7_qn), .T(in_1), .Q(out_9), .reset(button_1_out));  // open: Qn, preset, en
endmodule

module _1 (
  input  in_1,
  output out_2,
  output out_3,
  output out_4,
  output out_5,
  output out_6,
  output out_7,
  output out_8,
  output out_9
);

  wire button_1_out, clock_1_out, t_ff_1_qn, t_ff_2_qn, t_ff_3_qn, t_ff_4_qn, t_ff_5_qn, t_ff_6_qn, t_ff_7_qn;

  Clock clock_1 (.out(clock_1_out));
  Button button_1 (.out(button_1_out));
  T_Flip_Flop t_ff_1 (
    .clk(clock_1_out), .T(in_1), .Q(out_2), .Qn(t_ff_1_qn), .reset(button_1_out));  // open: preset, en
  T_Flip_Flop t_ff_2 (.clk(t_ff_1_qn), .T(in_1), .Q(out_3), .Qn(t_ff_2_qn), .reset(button_1_out));  // open: preset, en
  T_Flip_Flop t_ff_3 (.clk(t_ff_2_qn), .T(in_1), .Q(out_4), .Qn(t_ff_3_qn), .reset(button_1_out));  // open: preset, en
  T_Flip_Flop t_ff_4 (.clk(t_ff_3_qn), .T(in_1), .Q(out_5), .Qn(t_ff_4_qn), .reset(button_1_out));  // open: preset, en
  T_Flip_Flop t_ff_5 (.clk(t_ff_4_qn), .T(in_1), .Q(out_6), .Qn(t_ff_5_qn), .reset(button_1_out));  // open: preset, en
  T_Flip_Flop t_ff_6 (.clk(t_ff_5_qn), .T(in_1), .Q(out_7), .Qn(t_ff_6_qn), .reset(button_1_out));  // open: preset, en
  T_Flip_Flop t_ff_7 (.clk(t_ff_6_qn), .T(in_1), .Q(out_8), .Qn(t_ff_7_qn), .reset(button_1_out));  // open: preset, en
  T_Flip_Flop t_ff_8 (.clk(t_ff_7_qn), .T(in_1), .Q(out_9), .reset(button_1_out));  // open: Qn, preset, en
endmodule
