// Logisim project 13.02.24 умнжитьль дв. чисел.circ as structural Verilog: 1 circuit, main circuit main
module main (
  input  _2,
  input  in_2,
  input  in_3,
  input  _2_2,
  input  _1,
  input  _0,
  input  in_7,
  input  in_8,
  output _5,
  output _4,
  output _3,
  output _2_3,
  output _1_2,
  output _0_2
);

  wire _2_out, _3_out, _4_out, _5_out, _6_out, _7_out, _8_out, _9_out, and_1_out, and_2_out, and_3_out,
       and_4_out, and_5_out, and_6_out, and_7_out, and_8_out, xor_2_out, xor_3_out, xor_4_out, xor_5_out,
       xor_7_out, xor_8_out, xor_10_out;

  and u__1 (_0_2, in_3, _0);
  and u__2 (_2_out, in_2, _0);
  and u__3 (_3_out, _2, _0);
  and u__4 (_4_out, in_3, _1);
  and u__5 (_5_out, in_2, _1);
  and _6 (_6_out, _2, _1);
  and _7 (_7_out, in_3, _2_2);
  and _8 (_8_out, in_2, _2_2);
  and _9 (_9_out, _2, _2_2);
  xor xor_1 (_1_2, _2_out, _4_out);
  and and_1 (and_1_out, _2_out, _4_out);
  xor xor_2 (xor_2_out, _3_out, _5_out);
  and and_2 (and_2_out, _3_out, _5_out);
  xor xor_3 (xor_3_out, and_1_out, xor_2_out);
  and and_3 (and_3_out, and_1_out, xor_2_out);
  xor xor_4 (xor_4_out, and_3_out, and_2_out);
  xor xor_5 (xor_5_out, xor_4_out, _6_out);
  and and_4 (and_4_out, xor_4_out, _6_out);
  xor xor_6 (_2_3, xor_3_out, _7_out);
  and and_5 (and_5_out, xor_3_out, _7_out);
  xor xor_7 (xor_7_out, xor_5_out, _8_out);
  and and_6 (and_6_out, xor_5_out, _8_out);
  xor xor_8 (xor_8_out, and_4_out, _9_out);
  and and_7 (and_7_out, and_4_out, _9_out);
  xor xor_9 (_3, and_5_out, xor_7_out);
  and and_8 (and_8_out, and_5_out, xor_7_out);
  xor xor_10 (xor_10_out, and_8_out, and_6_out);
  xor xor_11 (_4, xor_10_out, xor_8_out);
  and and_9 (_5, xor_8_out, and_7_out);

  // Notes on the sheet:
  //   1
  //   0
endmodule
