// Logisim project flfybt 1.circ as structural Verilog: 1 circuit, main circuit main
module main (
);

  wire and_1_out, and_2_out, button_1_out, clock_1_out, decoder_1_out0, decoder_1_out1, decoder_1_out2,
       decoder_1_out3, decoder_1_out4, decoder_1_out5, decoder_1_out6, decoder_1_out7, demultiplexer_1_out0,
       demultiplexer_1_out1, demultiplexer_1_out2, demultiplexer_1_out3, demultiplexer_1_out4,
       demultiplexer_1_out5, demultiplexer_1_out6, demultiplexer_1_out7, multiplexer_1_out, undriven,
       undriven_2;
  wire [2:0] counter_1_q, counter_2_q;
  wire [7:0] random_1_out, register_1_q, register_2_q;

  Clock clock_1 (.out(clock_1_out));
  Random random_1 (.clk(and_1_out), .next(and_1_out), .out(random_1_out));  // open: clr
  Counter #(.width(3), .max('h7)) counter_1 (
    .count(clock_1_out), .Q(counter_1_q), .clk(clock_1_out), .clr(and_1_out));  // open: load, D, carry
  Register register_1 (.D(random_1_out), .en(undriven), .Q(register_1_q), .clk(clock_1_out));  // open: clr
  Multiplexer #(.select(3), .enable("false")) multiplexer_1 (
    .in0(register_1_q[0]), .in1(register_1_q[1]), .in2(register_1_q[2]), .in3(register_1_q[3]),
    .in4(register_1_q[4]), .in5(register_1_q[5]), .in6(register_1_q[6]), .in7(register_1_q[7]),
    .out(multiplexer_1_out), .sel({counter_1_q[0], counter_1_q[1], counter_1_q[2]}));
  and and_1 (and_1_out, counter_1_q[0], undriven);
  Counter #(.width(3), .max('h7)) counter_2 (
    .count(clock_1_out), .Q(counter_2_q), .clk(clock_1_out), .clr(and_2_out));  // open: load, D, carry
  Demultiplexer #(.select(3), .enable("false")) demultiplexer_1 (
    .out0(demultiplexer_1_out0), .out1(demultiplexer_1_out1), .out2(demultiplexer_1_out2),
    .out3(demultiplexer_1_out3), .out4(demultiplexer_1_out4), .out5(demultiplexer_1_out5),
    .out6(demultiplexer_1_out6), .out7(demultiplexer_1_out7), .in(multiplexer_1_out),
    .sel({counter_2_q[0], counter_2_q[1], counter_2_q[2]}));
  and and_2 (and_2_out, counter_2_q[0], undriven_2);
  Button button_1 (.out(button_1_out));
  Decoder #(.select(3)) decoder_1 (
    .out0(decoder_1_out0), .out1(decoder_1_out1), .out2(decoder_1_out2), .out3(decoder_1_out3),
    .out4(decoder_1_out4), .out5(decoder_1_out5), .out6(decoder_1_out6), .out7(decoder_1_out7),
    .sel({counter_2_q[0], counter_2_q[1], counter_2_q[2]}));  // open: en
  Register #(.width(1)) register_2 (
    .D(demultiplexer_1_out0), .en(decoder_1_out0), .Q(register_2_q[0]), .clk(clock_1_out), .clr(button_1_out));
  Register #(.width(1)) register_3 (
    .D(demultiplexer_1_out1), .en(decoder_1_out1), .Q(register_2_q[1]), .clk(clock_1_out), .clr(button_1_out));
  Register #(.width(1)) register_4 (
    .D(demultiplexer_1_out2), .en(decoder_1_out2), .Q(register_2_q[2]), .clk(clock_1_out), .clr(button_1_out));
  Register #(.width(1)) register_5 (
    .D(demultiplexer_1_out3), .en(decoder_1_out3), .Q(register_2_q[3]), .clk(clock_1_out), .clr(button_1_out));
  Register #(.width(1)) register_6 (
    .D(demultiplexer_1_out4), .en(decoder_1_out4), .Q(register_2_q[4]), .clk(clock_1_out), .clr(button_1_out));
  Register #(.width(1)) register_7 (
    .D(demultiplexer_1_out5), .en(decoder_1_out5), .Q(register_2_q[5]), .clk(clock_1_out), .clr(button_1_out));
  Register #(.width(1)) register_8 (
    .D(demultiplexer_1_out6), .en(decoder_1_out6), .Q(register_2_q[6]), .clk(clock_1_out), .clr(button_1_out));
  Register #(.width(1)) register_9 (
    .D(demultiplexer_1_out7), .en(decoder_1_out7), .Q(register_2_q[7]), .clk(clock_1_out), .clr(button_1_out));
  // Probe on register_2_q
endmodule
