// Logisim project задание 1-3.circ as structural Verilog: 2 circuits, main circuit 1
module _1 (
  input  [3:0] in_1,
  output out_2,
  output out_3,
  output out_4,
  output out_5,
  output out_6,
  output out_7,
  output out_8
);

  wire button_1_out, button_2_out, button_3_out, button_4_out, button_5_out, button_6_out, button_7_out,
       button_8_out, button_9_out, t_ff_1_q, t_ff_2_q, t_ff_3_q, t_ff_4_q, t_ff_5_q, t_ff_6_q, t_ff_7_q,
       t_ff_8_q, t_ff_9_q;

  Button button_1 (.out(button_1_out));
  Button button_2 (.out(button_2_out));
  T_Flip_Flop t_ff_1 (.clk(button_1_out), .T(button_1_out), .Q(t_ff_1_q));  // open: Qn, preset, reset, en
  T_Flip_Flop t_ff_2 (.clk(button_2_out), .T(button_2_out), .Q(t_ff_2_q));  // open: Qn, preset, reset, en
  Button button_3 (.out(button_3_out));
  Multiplexer #(.select(4), .width(7), .enable("false")) multiplexer_1 (
    .in0(7'b1110111), .in1(7'b1000001), .in2(7'b0111011), .in3(7'b1101011), .in4(7'b1001101),
    .in5(7'b1101110), .in6(7'b1111110), .in7(7'b1000011), .in8({7{1'b1}}), .in9(7'b1101111),
    .in10(7'b1011111), .in11(7'b1111100), .in12(7'b0110110), .in13(7'b1111001), .in14(7'b0111110),
    .in15(7'b0011110), .out({out_2, out_3, out_4, out_5, out_6, out_7, out_8}), .sel(in_1));
  Button button_4 (.out(button_4_out));
  T_Flip_Flop t_ff_3 (.clk(button_3_out), .T(button_3_out), .Q(t_ff_3_q));  // open: Qn, preset, reset, en
  Button button_5 (.out(button_5_out));
  Button button_6 (.out(button_6_out));
  T_Flip_Flop t_ff_4 (.clk(button_4_out), .T(button_4_out), .Q(t_ff_4_q));  // open: Qn, preset, reset, en
  _7_Segment_Display u_7_segment_display_1 (
    .g(out_5), .f(out_6), .a(out_7), .b(out_8), .e(out_4), .d(out_3), .c(out_2), .dp(t_ff_5_q));
  T_Flip_Flop t_ff_5 (.clk(button_5_out), .T(button_5_out), .Q(t_ff_5_q));  // open: Qn, preset, reset, en
  Button button_7 (.out(button_7_out));
  T_Flip_Flop t_ff_6 (.clk(button_6_out), .T(button_6_out), .Q(t_ff_6_q));  // open: Qn, preset, reset, en
  Button button_8 (.out(button_8_out));
  T_Flip_Flop t_ff_7 (.clk(button_7_out), .T(button_7_out), .Q(t_ff_7_q));  // open: Qn, preset, reset, en
  Button button_9 (.out(button_9_out));
  T_Flip_Flop t_ff_8 (.clk(button_8_out), .T(button_8_out), .Q(t_ff_8_q));  // open: Qn, preset, reset, en
  _7_Segment_Display u_7_segment_display_2 (
    .g(t_ff_4_q), .f(t_ff_6_q), .a(t_ff_7_q), .b(t_ff_8_q), .e(t_ff_3_q), .d(t_ff_2_q), .c(t_ff_1_q),
    .dp(t_ff_9_q));
  T_Flip_Flop t_ff_9 (.clk(button_9_out), .T(button_9_out), .Q(t_ff_9_q));  // open: Qn, preset, reset, en
endmodule

module _2 (
  input  [6:0] in_1
);

  _7_Segment_Display u_7_segment_display_1 (
    .g(in_1[3]), .f(in_1[2]), .a(in_1[1]), .b(in_1[0]), .e(in_1[2]), .d(in_1[1]), .c(in_1[0]));  // open: dp
  _1 u_1_1 (
    .out_2(in_1[0]), .out_3(in_1[1]), .out_4(in_1[2]), .out_5(in_1[3]), .out_6(in_1[4]), .out_7(in_1[5]),
    .out_8(in_1[6]));  // open: in_1
  // Pins of 3 and 4 and 7 bits meet at in_1
endmodule
