// Logisim project карташев 1-3.circ as structural Verilog: 3 circuits, main circuit 1
module _1 (
  input  [3:0] in_1,
  output out_2,
  output out_3,
  output out_4,
  output out_5,
  output out_6,
  output out_7,
  output out_8
);

  wire button_1_out, t_ff_1_q;

  Multiplexer #(.select(4), .width(7), .enable("false")) multiplexer_1 (
    .in0(7'b1110111), .in1(7'b1000001), .in2(7'b0111011), .in3(7'b1101011), .in4(7'b1001101),
    .in5(7'b1101110), .in6(7'b1111110), .in7(7'b1000011), .in8({7{1'b1}}), .in9(7'b1101111),
    .in10(7'b1011111), .in11(7'b1111100), .in12(7'b0110110), .in13(7'b1111001), .in14(7'b0111110),
    .in15(7'b0011110), .out({out_8, out_7, out_6, out_5, out_4, out_3, out_2}), .sel(in_1));
  Button button_1 (.out(button_1_out));
  _7_Segment_Display u_7_segment_display_1 (
    .g(out_5), .f(out_4), .a(out_3), .b(out_2), .e(out_6), .d(out_7), .c(out_8), .dp(t_ff_1_q));
  T_Flip_Flop t_ff_1 (.clk(button_1_out), .T(button_1_out), .Q(t_ff_1_q));  // open: Qn, preset, reset, en
endmodule

module _2 (
  input  [15:0] in_1,
  output [6:0] out_2,
  output [6:0] out_3,
  output [6:0] out_4,
  output [6:0] out_5,
  output [6:0] out_6
);

  wire [3:0] bit_extender_1_out, bit_extender_2_out, bit_extender_3_out, bit_extender_4_out,
       bit_extender_5_out;
  wire [15:0] divider_1_out, divider_1_rem, divider_2_out, divider_2_rem, divider_3_out, divider_3_rem,
       divider_4_out, divider_4_rem;

  _7_Segment_Display u_7_segment_display_1 (
    .g(out_2[3]), .f(out_2[2]), .a(out_2[1]), .b(out_2[0]), .e(out_2[2]), .d(out_2[1]), .c(out_2[0]));  // open: dp
  _1 u_1_1 (
    .in_1(bit_extender_1_out), .out_2(out_2[0]), .out_3(out_2[1]), .out_4(out_2[2]), .out_5(out_2[3]),
    .out_6(out_2[4]), .out_7(out_2[5]), .out_8(out_2[6]));
  _7_Segment_Display u_7_segment_display_2 (
    .g(out_3[3]), .f(out_3[2]), .a(out_3[1]), .b(out_3[0]), .e(out_3[2]), .d(out_3[1]), .c(out_3[0]));  // open: dp
  _1 u_1_2 (
    .in_1(bit_extender_2_out), .out_2(out_3[0]), .out_3(out_3[1]), .out_4(out_3[2]), .out_5(out_3[3]),
    .out_6(out_3[4]), .out_7(out_3[5]), .out_8(out_3[6]));
  Divider #(.width(16)) divider_1 (.a(in_1), .b(16'h2710), .out(divider_1_out), .rem(divider_1_rem));  // open: upper
  _7_Segment_Display u_7_segment_display_3 (
    .g(out_4[3]), .f(out_4[2]), .a(out_4[1]), .b(out_4[0]), .e(out_4[2]), .d(out_4[1]), .c(out_4[0]));  // open: dp
  _1 u_1_3 (
    .in_1(bit_extender_3_out), .out_2(out_4[0]), .out_3(out_4[1]), .out_4(out_4[2]), .out_5(out_4[3]),
    .out_6(out_4[4]), .out_7(out_4[5]), .out_8(out_4[6]));
  Bit_Extender #(.in_width(16), .out_width(4)) bit_extender_1 (.in(divider_1_out), .out(bit_extender_1_out));
  Divider #(.width(16)) divider_2 (
    .a(divider_1_rem), .b(16'h3e8), .out(divider_2_out), .rem(divider_2_rem));  // open: upper
  Bit_Extender #(.in_width(16), .out_width(4)) bit_extender_2 (.in(divider_2_out), .out(bit_extender_2_out));
  Divider #(.width(16)) divider_3 (
    .a(divider_2_rem), .b(16'h64), .out(divider_3_out), .rem(divider_3_rem));  // open: upper
  _7_Segment_Display u_7_segment_display_4 (
    .g(out_5[3]), .f(out_5[2]), .a(out_5[1]), .b(out_5[0]), .e(out_5[2]), .d(out_5[1]), .c(out_5[0]));  // open: dp
  _1 u_1_4 (
    .in_1(bit_extender_4_out), .out_2(out_5[0]), .out_3(out_5[1]), .out_4(out_5[2]), .out_5(out_5[3]),
    .out_6(out_5[4]), .out_7(out_5[5]), .out_8(out_5[6]));
  Bit_Extender #(.in_width(16), .out_width(4)) bit_extender_3 (.in(divider_3_out), .out(bit_extender_3_out));
  Divider #(.width(16)) divider_4 (
    .a(divider_3_rem), .b(16'ha), .out(divider_4_out), .rem(divider_4_rem));  // open: upper
  Bit_Extender #(.in_width(16), .out_width(4)) bit_extender_4 (.in(divider_4_out), .out(bit_extender_4_out));
  Bit_Extender #(.in_width(16), .out_width(4)) bit_extender_5 (.in(divider_4_rem), .out(bit_extender_5_out));
  _1 u_1_5 (
    .in_1(bit_extender_5_out), .out_2(out_6[0]), .out_3(out_6[1]), .out_4(out_6[2]), .out_5(out_6[3]),
    .out_6(out_6[4]), .out_7(out_6[5]), .out_8(out_6[6]));
  _7_Segment_Display u_7_segment_display_5 (
    .g(out_6[3]), .f(out_6[2]), .a(out_6[1]), .b(out_6[0]), .e(out_6[4]), .d(out_6[5]), .c(out_6[6]));  // open: dp
endmodule

module _3 (
);

  wire _1_out, _2_out, _3_out, _4_out, and_1_out, buffer_1_out, buffer_2_out, buffer_3_out, buffer_4_out,
       comparator_1_eq, not_1_out, or_1_out, or_2_out;
  wire [6:0] n2_1_out_2, n2_1_out_3, n2_1_out_4, n2_1_out_5, n2_1_out_6, n2_2_out_2, n2_2_out_3, n2_2_out_4,
       n2_2_out_5, n2_2_out_6;
  wire [15:0] adder_1_out, adder_2_out, divider_1_out, multiplexer_1_out, multiplexer_2_out,
       multiplier_1_out, register_1_q, register_2_q, subtractor_1_out;

  Multiplexer #(.width(16)) multiplexer_1 (
    .in0(subtractor_1_out), .in1(adder_1_out), .out(multiplexer_1_out), .sel(_2_out));  // open: en
  Register #(.width(16)) register_1 (
    .D(multiplexer_1_out), .en(buffer_1_out), .Q(register_1_q), .clk(buffer_1_out));  // open: clr
  buf buffer_1 (buffer_1_out, buffer_2_out);
  buf buffer_2 (buffer_2_out, or_1_out);
  or or_1 (or_1_out, _2_out, _1_out);
  Button _1 (.out(_1_out));
  _7_Segment_Display u_7_segment_display_1 (
    .g(n2_1_out_2[3]), .f(n2_1_out_2[2]), .a(n2_1_out_2[1]), .b(n2_1_out_2[0]), .e(n2_1_out_2[4]),
    .d(n2_1_out_2[5]), .c(n2_1_out_2[6]));  // open: dp
  _7_Segment_Display u_7_segment_display_2 (
    .g(n2_1_out_3[3]), .f(n2_1_out_3[2]), .a(n2_1_out_3[1]), .b(n2_1_out_3[0]), .e(n2_1_out_3[4]),
    .d(n2_1_out_3[5]), .c(n2_1_out_3[6]));  // open: dp
  _2 u_2_1 (
    .in_1(register_1_q), .out_2(n2_1_out_2), .out_3(n2_1_out_3), .out_4(n2_1_out_4), .out_5(n2_1_out_5),
    .out_6(n2_1_out_6));
  Subtractor #(.width(16)) subtractor_1 (.a(register_1_q), .b(adder_2_out), .out(subtractor_1_out));  // open: bin, bout
  Adder #(.width(16)) adder_1 (.a(register_1_q), .b(adder_2_out), .out(adder_1_out));  // open: cin, cout
  Button _2 (.out(_2_out));
  _7_Segment_Display u_7_segment_display_3 (
    .g(n2_1_out_4[3]), .f(n2_1_out_4[2]), .a(n2_1_out_4[1]), .b(n2_1_out_4[0]), .e(n2_1_out_4[4]),
    .d(n2_1_out_4[5]), .c(n2_1_out_4[6]));  // open: dp
  Register #(.width(16)) register_2 (
    .D(multiplexer_2_out), .en(buffer_4_out), .Q(register_2_q), .clk(buffer_4_out));  // open: clr
  Multiplexer #(.width(16)) multiplexer_2 (
    .in0(divider_1_out), .in1(multiplier_1_out), .out(multiplexer_2_out), .sel(and_1_out));  // open: en
  or or_2 (or_2_out, _3_out, and_1_out);
  Button _3 (.out(_3_out));
  Button _4 (.out(_4_out));
  _7_Segment_Display u_7_segment_display_4 (
    .g(n2_1_out_5[3]), .f(n2_1_out_5[2]), .a(n2_1_out_5[1]), .b(n2_1_out_5[0]), .e(n2_1_out_5[4]),
    .d(n2_1_out_5[5]), .c(n2_1_out_5[6]));  // open: dp
  buf buffer_3 (buffer_3_out, or_2_out);
  buf buffer_4 (buffer_4_out, buffer_3_out);
  and and_1 (and_1_out, _4_out, not_1_out);
  not not_1 (not_1_out, comparator_1_eq);
  _7_Segment_Display u_7_segment_display_5 (
    .g(n2_1_out_6[3]), .f(n2_1_out_6[2]), .a(n2_1_out_6[1]), .b(n2_1_out_6[0]), .e(n2_1_out_6[4]),
    .d(n2_1_out_6[5]), .c(n2_1_out_6[6]));  // open: dp
  Adder #(.width(16)) adder_2 (.a(register_2_q), .b(16'h1), .out(adder_2_out));  // open: cin, cout
  _7_Segment_Display u_7_segment_display_6 (
    .g(n2_2_out_2[3]), .f(n2_2_out_2[2]), .a(n2_2_out_2[1]), .b(n2_2_out_2[0]), .e(n2_2_out_2[4]),
    .d(n2_2_out_2[5]), .c(n2_2_out_2[6]));  // open: dp
  _2 u_2_2 (
    .in_1(adder_2_out), .out_2(n2_2_out_2), .out_3(n2_2_out_3), .out_4(n2_2_out_4), .out_5(n2_2_out_5),
    .out_6(n2_2_out_6));
  Comparator #(.width(16)) comparator_1 (.a(adder_2_out), .b(16'ha), .eq(comparator_1_eq));  // open: gt, lt
  _7_Segment_Display u_7_segment_display_7 (
    .g(n2_2_out_3[3]), .f(n2_2_out_3[2]), .a(n2_2_out_3[1]), .b(n2_2_out_3[0]), .e(n2_2_out_3[4]),
    .d(n2_2_out_3[5]), .c(n2_2_out_3[6]));  // open: dp
  Divider #(.width(16)) divider_1 (.a(adder_2_out), .b(16'ha), .out(divider_1_out));  // open: upper, rem
  Multiplier #(.width(16)) multiplier_1 (.a(adder_2_out), .b(16'ha), .out(multiplier_1_out));  // open: cin, cout
  _7_Segment_Display u_7_segment_display_8 (
    .g(n2_2_out_5[3]), .f(n2_2_out_5[2]), .a(n2_2_out_5[1]), .b(n2_2_out_5[0]), .e(n2_2_out_5[4]),
    .d(n2_2_out_5[5]), .c(n2_2_out_5[6]));  // open: dp
  _7_Segment_Display u_7_segment_display_9 (
    .g(n2_2_out_4[3]), .f(n2_2_out_4[2]), .a(n2_2_out_4[1]), .b(n2_2_out_4[0]), .e(n2_2_out_4[4]),
    .d(n2_2_out_4[5]), .c(n2_2_out_4[6]));  // open: dp
  _7_Segment_Display u_7_segment_display_10 (
    .g(n2_2_out_6[3]), .f(n2_2_out_6[2]), .a(n2_2_out_6[1]), .b(n2_2_out_6[0]), .e(n2_2_out_6[4]),
    .d(n2_2_out_6[5]), .c(n2_2_out_6[6]));  // open: dp
endmodule
